# Fritzing sketch computer-power-supply (saved by Fritzing 0.9.3b)
breadboards: 1

parts:
  F1 = Resettable Fuse PTC [package=0603]
  C1 = Electrolytic Capacitor [capacitance=100µF package="300 mil [THT, electrolytic]"]
  C2 = Electrolytic Capacitor [capacitance=100µF package="300 mil [THT, electrolytic]"]
  C3 = Electrolytic Capacitor [capacitance=100µF package="300 mil [THT, electrolytic]"]
  C4 = Electrolytic Capacitor [capacitance=100µF package="300 mil [THT, electrolytic]"]
  D1 = Rectifier Diode [part_number=1N4001 package="300 mil [THT]"]
  D2 = Rectifier Diode [part_number=1N4001 package="300 mil [THT]"]
  D3 = Rectifier Diode [part_number=1N4001 package="300 mil [THT]"]
  D4 = Rectifier Diode [part_number=1N4001 package="300 mil [THT]"]
  V1 = AC Power

nets:
  Can be replaced with breaker or non-resettable fuse: F1.1, V1.V+
  Investigate: 4001 is too low voltage rating // 4005 or 4006 was suggested/The 1n-400x are also only good for 1amp max current: F1.2, D1.anode, D2.anode, D3.cathode, D4.cathode, V1.V-
  N1: C1.-, C2.-, C3.-, C4.-
  Verify capacitor to use: C1.+, C2.+, C3.+, C4.+
  LOAD: D1.cathode, D2.cathode, D3.anode, D4.anode

notes:
  Rectification of input

custom parts:
  Resettable Fuse PTC: Resettable Fuse PTC Resettable Fuse. Spark Fun Electronics SKU : COM-08357
  AC Power: A generic ac power symbol
